# Fritzing sketch atmega settings (saved by Fritzing 0.9.5d)
breadboards: 4

parts:
  IC3 = Atmega8 [package=dil28-3-simon]
  XTAL1 = Crystal [frequency="16 Mhz" package=THT]
  VCC1 = Battery block 9V
  C1 = Capacitor [package=cap-pth-small2]
  C2 = Capacitor [package=cap-pth-small2]
  U4 = Voltage Regulator - 5V [package="DPak [SMD]"]
  U5 = Voltage Regulator [package=to220-adj]
  C4 = Electrolytic Capacitor [capacitance=10μF package="0605 [SMD, electrolytic]"]
  C5 = Capacitor [package=cap-pth-small2]
  C6 = Electrolytic Capacitor [capacitance=10μF package="0605 [SMD, electrolytic]"]
  R2 = Resistor [tolerance=±5% resistance=220 package="2010 [SMD]"]
  R3 = Resistor [tolerance=±5% resistance=220 package="2010 [SMD]"]
  R4 = Resistor [tolerance=±5% resistance=220 package="2010 [SMD]"]
  S1 = Pushbutton [package=THT]
  R5 = Resistor [tolerance=±5% resistance=220 package=THT]

nets:
  N1: IC3.PC6(_RESET), S1.leg0, R5.Pin_1
  N2: IC3.VCC, U4.output_voltage, R5.Pin_0
  GND: IC3.GND, VCC1.-, C1.2, C2.1, U4.GND, C5.1, C6.-, R4.Pin_0, S1.leg1
  N3: IC3.PB6(XTAL1_TOSC1), XTAL1.pin_0, C2.2
  N4: IC3.PB7(XTAL2_TOSC2), XTAL1.pin_1, C1.1
  N5: VCC1.+, U4.input_voltage, U5.OUT, C4.+
  N6: U5.ADJ, C4.-, R2.Pin_1, R3.Pin_0
  N7: U5.IN, C5.2, C6.+, R3.Pin_1
  N8: R2.Pin_0, R4.Pin_1

notes:
  lm317
  ground 3.3v input
  L7805
  input ground 5v

custom parts:
  Atmega8: MICROCONTROLLER 8 Kbytes FLASH 1 kbytes SRAM 512 bytes EEPROM USART 4-channel 10 bit ADC 2-channel 8 bit ADC
