# Fritzing sketch atmega328 and motor driver (saved by Fritzing 0.9.5d)
breadboards: 3

parts:
  IC3 = Atmega8 [package=dil28-3-simon]
  L298N1 = L298N DC motor driver
  M1 = DC Motor
  XTAL1 = Crystal [frequency="16 Mhz" package=THT]
  VCC1 = Battery block 9V
  C1 = Capacitor [package=cap-pth-small2]
  C2 = Capacitor [package=cap-pth-small2]
  U4 = Voltage Regulator - 5V [package="DPak [SMD]"]
  S2 = Pushbutton [package=THT]
  R6 = Resistor [tolerance=±5% resistance=220 package=THT]

nets:
  N1: IC3.PC6(_RESET), S2.leg0, R6.Pin_1
  N2: IC3.PD3(INT1), L298N1.ENA
  N3: IC3.VCC, U4.output_voltage, R6.Pin_0
  GND: IC3.GND, L298N1.GND, VCC1.-, C1.2, C2.1, U4.GND, S2.leg1
  N4: IC3.PB6(XTAL1_TOSC1), XTAL1.pin_0, C2.2
  N5: IC3.PB7(XTAL2_TOSC2), XTAL1.pin_1, C1.1
  N6: IC3.PC0(ADC0), L298N1.IN2
  N7: IC3.PC1(ADC1), L298N1.5V, L298N1.IN1
  N8: L298N1.OUT1, M1.pin_2
  N9: L298N1.OUT2, M1.pin_1
  N10: L298N1.12V, VCC1.+, U4.input_voltage

notes:
  L298N
  PC1 IN1 green
  PC0 IN2 orange
  PD3 ENA white
  out1 red
  out2 black
  L7805
  input ground 5v

custom parts:
  Atmega8: MICROCONTROLLER 8 Kbytes FLASH 1 kbytes SRAM 512 bytes EEPROM USART 4-channel 10 bit ADC 2-channel 8 bit ADC
  L298N DC motor driver: 2x DC motor driver with 78M05 positive voltage regulator (7..35 V) L298N: max 46 V, 2 A Set 5 V Enable jumper to enable 5 V regultor (needed for the L298N) and +5 V output at screw terminal or supply external +5 V at screw terminal Set ENA and/or ENB to +5 V to enable motor permanently or supply ENA and/or ENB with PWM signal IN1 and IN2 set rotation directory for motor A (OUT1/OUT2) IN2 and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
