# Fritzing sketch curcite block (saved by Fritzing 0.9.5d)
breadboards: 9

parts:
  IC3 = Atmega8 [package=dil28-3-simon]
  L298N1 = L298N DC motor driver
  M1 = DC Motor
  XTAL1 = Crystal [frequency="16 Mhz" package=THT]
  VCC1 = Battery block 9V
  C1 = Capacitor [package=cap-pth-small2]
  C2 = Capacitor [package=cap-pth-small2]
  HC-SR04_Sensor_1 = HC-SR04 Ultrasonic Distance Sensor  # not connected
  J1 = Basic Servo
  U1 = RFID RC522 SIP - 8 pins [chip_label="RFID RC522" package="SIP (Single Inline) [THT]"]
  SG1 = Buzzer 12mm [package=buzzer-12mm-ns-kit]
  U2 = RFID RC522 SIP - 8 pins [chip_label="RFID RC522" package="SIP (Single Inline) [THT]"]
  U3 = RFID RC522 SIP - 8 pins [chip_label="RFID RC522" package="SIP (Single Inline) [THT]"]
  Part1 = NRF24L01+ Breakout Board
  Part2 = NRF24L01+ Breakout Board
  Jetson_Nano1 = Jetson Nano
  R1 = Resistor [tolerance=±5% resistance=220 package="2010 [SMD]"]
  C3 = Electrolytic Capacitor [capacitance=10μF package="0605 [SMD, electrolytic]"]
  VCC2 = Battery block 9V
  J2 = Basic Servo
  U4 = Voltage Regulator - 5V [package="DPak [SMD]"]
  U5 = Voltage Regulator [package=to220-adj]
  C4 = Electrolytic Capacitor [capacitance=10μF package="0605 [SMD, electrolytic]"]
  C5 = Capacitor [package=cap-pth-small2]
  C6 = Electrolytic Capacitor [capacitance=10μF package="0605 [SMD, electrolytic]"]
  R2 = Resistor [tolerance=±5% resistance=220 package="2010 [SMD]"]
  R3 = Resistor [tolerance=±5% resistance=220 package="2010 [SMD]"]
  R4 = Resistor [tolerance=±5% resistance=220 package="2010 [SMD]"]
  R5 = Resistor [tolerance=±5% resistance=220 package=THT]
  S1 = Pushbutton [package=THT]
  R6 = Resistor [tolerance=±5% resistance=220 package=THT]
  D1 = Rectifier Diode [part_number=1N4001 package="300 mil [THT]"]
  D2 = Rectifier Diode [part_number=1N4001 package="300 mil [THT]"]

nets:
  N1: IC3.PC6(_RESET), R5.Pin_1, S1.leg0
  N2: IC3.PD2(INT0), Part2.IRQ
  N3: IC3.PD3(INT1), L298N1.ENA
  N4: IC3.VCC, U4.output_voltage, R5.Pin_0
  GND: IC3.GND, L298N1.GND, VCC1.-, C1.2, C2.1, U4.GND, C5.1, C6.-, R4.Pin_0, S1.leg1
  N5: IC3.PB6(XTAL1_TOSC1), XTAL1.pin_0, C2.2
  N6: IC3.PB7(XTAL2_TOSC2), XTAL1.pin_1, C1.1
  N7: IC3.PB1(OC1A), Part2.CS
  N8: IC3.PB2(SS_OC1B), Part2.CE
  N9: IC3.PB3(MOSI_OC2), Part2.MOSI
  N10: IC3.PB4(MISO), Part2.MISO
  N11: IC3.PB5(SCK), Part2.SCK
  N12: IC3.PC0(ADC0), L298N1.IN2
  N13: IC3.PC1(ADC1), L298N1.5V, L298N1.IN1
  N14: L298N1.OUT1, M1.pin_2
  N15: L298N1.OUT2, M1.pin_1
  N16: L298N1.12V, VCC1.+, U4.input_voltage, U5.OUT, C4.+
  GND_2: J1.gnd, U1.GND, SG1.2, U2.GND, U3.GND, Part1.GND, Jetson_Nano1.GPIO19, C3.-, VCC2.-, J2.gnd, R6.Pin_0
  VCC: J1.vcc, VCC2.+, J2.vcc
  N17: J1.pulse, Jetson_Nano1.GPIO14
  N18: U1.NSS, Jetson_Nano1.GPIO11
  N19: U1.SCK, Part1.SCK, Jetson_Nano1.ID_SC
  N20: U1.MOSI, Part1.MOSI, Jetson_Nano1.5V
  N21: U1.MISO, Part1.MISO, Jetson_Nano1.GPIO10
  N22: U1.RST, U2.RST, U3.RST, Jetson_Nano1.GPIO5
  VCC_2: U1.VCC, U2.VCC, U3.VCC, Part1.VCC, Jetson_Nano1.GPIO21, R1.Pin_1, C3.+
  N23: SG1.1, Jetson_Nano1.GPIO15
  N24: U2.NSS, Jetson_Nano1.GPIO22
  N25: U2.SCK, U3.SCK, Jetson_Nano1.GPIO24
  N26: U2.MOSI, U3.MOSI, Jetson_Nano1.GPIO25
  N27: U2.MISO, D1.anode
  3V3: U3.NSS, Part1.IRQ, Jetson_Nano1.3v3, Jetson_Nano1.3V3, R1.Pin_0
  N28: U3.MISO, D2.anode
  N29: Part1.CS, Jetson_Nano1.GND, J2.pulse, R6.Pin_1, D1.cathode, D2.cathode
  N30: Part2.GND, U5.ADJ, C4.-, R2.Pin_1, R3.Pin_0
  N31: Part2.VCC, U5.IN, C5.2, C6.+, R3.Pin_1
  N32: R2.Pin_0, R4.Pin_1

notes:
  spi 1
  23 clock white
  21 miso yellow
  19 mosi brown
  24 select0 green
  26 select1orange
  12 rest pink
  spi 2
  13 clock white
  22 miso yellow
  37 mosi brown
  18 select0 green
  16 select1orange
  12 rest pink
  NRF24
  40 IRQ blue
  RFID 2
  spi 1
  23 clock white
  21 miso yellow
  19 mosi brown
  26 select1orange
  12 rest pink
  RFID 1
  spi 1
  23 clock white
  21 miso yellow
  19 mosi brown
  24 select0 green
  12 rest pink
  NRF24
  spi 2
  13 clock white
  22 miso yellow
  37 mosi brown
  16 select1orange
  12 rest pink
  NRF24
  40 IRQ blue
  CE none
  spi 2
  13 clock white
  22 miso yellow
  37 mosi brown
  18 select0 green
  12 rest pink
  NRF24
  40 IRQ blue
  pwm0
  32 cyan
  pwm 1
  33 grey
  output buzzer
  31 brown
  servo motor 1
  pwm0
  32 cyan
  servo motor 2
  pwm 1
  33 grey
  output buzzer
  31 brown
  spi 1
  23 clock white
  21 miso yellow
  19 mosi brown
  24 select0 green
  26 select1orange
  12 rest pink
  *****************************
  spi 2
  13 clock white
  22 miso yellow
  37 mosi brown
  18 select0 green
  16 select1orange
  12 rest pink
  NRF24
  40 IRQ blue
  ***************************************
  pwm0
  32 cyan
  pwm 1
  33 grey
  output buzzer
  31 brown
  NRF24
  spi
  PB5 clock white
  PB4 miso yellow
  PB3 mosi brown
  PD2 IRQ blue
  PB2 select0 green
  PB1 ce grey
  L298N
  PC1 IN1 green
  PC0 IN2 orange
  PD3 ENA white
  out1 red
  out2 black
  lm317
  ground 3.3v input
  L7805
  input ground 5v

custom parts:
  Atmega8: MICROCONTROLLER 8 Kbytes FLASH 1 kbytes SRAM 512 bytes EEPROM USART 4-channel 10 bit ADC 2-channel 8 bit ADC
  L298N DC motor driver: 2x DC motor driver with 78M05 positive voltage regulator (7..35 V) L298N: max 46 V, 2 A Set 5 V Enable jumper to enable 5 V regultor (needed for the L298N) and +5 V output at screw terminal or supply external +5 V at screw terminal Set ENA and/or ENB to +5 V to enable motor permanently or supply ENA and/or ENB with PWM signal IN1 and IN2 set rotation directory for motor A (OUT1/OUT2) IN2 and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
  RFID RC522 SIP - 8 pins: A SIP stand-in part for RFID RC522 . With 8 pins on a 300 mil single inline package (SIP) footprint.
