# Fritzing sketch motor and buzzer (saved by Fritzing 0.9.5d)
breadboards: 1

parts:
  J1 = Basic Servo
  SG1 = Buzzer 12mm [package=buzzer-12mm-ns-kit]
  Jetson_Nano1 = Jetson Nano
  VCC2 = Battery block 9V
  J2 = Basic Servo

nets:
  GND: J1.gnd, SG1.2, VCC2.-, J2.gnd
  VCC: J1.vcc, VCC2.+, J2.vcc
  N1: J1.pulse, Jetson_Nano1.GPIO14
  N2: SG1.1, Jetson_Nano1.GPIO15
  N3: Jetson_Nano1.GND, J2.pulse

notes:
  pwm0
  32 cyan
  pwm 1
  33 grey
  output buzzer
  31 brown
  servo motor 1
  pwm0
  32 cyan
  servo motor 2
  pwm 1
  33 grey
  output buzzer
  31 brown
