# Fritzing sketch nrf24 (saved by Fritzing 0.9.5d)
breadboards: 2

parts:
  Part1 = NRF24L01+ Breakout Board
  Jetson_Nano1 = Jetson Nano
  R1 = Resistor [tolerance=±5% resistance=220 package="2010 [SMD]"]
  C3 = Electrolytic Capacitor [capacitance=10μF package="0605 [SMD, electrolytic]"]

nets:
  N1: Part1.GND, Jetson_Nano1.GPIO19, C3.-
  N2: Part1.VCC, Jetson_Nano1.GPIO21, R1.Pin_1, C3.+
  N3: Part1.CS, Jetson_Nano1.GND
  N4: Part1.SCK, Jetson_Nano1.ID_SC
  N5: Part1.MOSI, Jetson_Nano1.5V
  N6: Part1.MISO, Jetson_Nano1.GPIO10
  N7: Part1.IRQ, Jetson_Nano1.3v3, R1.Pin_0

notes:
  spi 2
  13 clock white
  22 miso yellow
  37 mosi brown
  18 select0 green
  16 select1orange
  12 rest pink
  NRF24
  40 IRQ blue
  NRF24
  spi 2
  13 clock white
  22 miso yellow
  37 mosi brown
  16 select1orange
  12 rest pink
  NRF24
  40 IRQ blue
  CE none
