# Fritzing sketch rfid_1 (saved by Fritzing 0.9.5d)
breadboards: 4

parts:
  IC3 = Atmega8 [package=dil28-3-simon]
  L298N1 = L298N DC motor driver
  M1 = DC Motor
  XTAL1 = Crystal [frequency="16 Mhz" package=THT]
  VCC1 = Battery block 9V
  C1 = Capacitor [package=cap-pth-small2]
  C2 = Capacitor [package=cap-pth-small2]
  HC-SR04_Sensor_1 = HC-SR04 Ultrasonic Distance Sensor  # not connected
  U3 = RFID RC522 SIP - 8 pins [chip_label="RFID RC522" package="SIP (Single Inline) [THT]"]
  IC4 = Voltage Regulator [package=to-220-alt]
  Part2 = NRF24L01+ Breakout Board
  Jetson_Nano1 = Jetson Nano
  R1 = Resistor [tolerance=±5% resistance=220 package="2010 [SMD]"]  # not connected

nets:
  VCC: IC3.VCC, L298N1.5V#7, IC4.OUT, Part2.VCC
  GND: IC3.GND, L298N1.GND, VCC1.-, C1.2, C2.1, IC4.GND, Part2.GND
  N1: IC3.PB6(XTAL1_TOSC1), XTAL1.pin_0, C2.2
  N2: IC3.PB7(XTAL2_TOSC2), XTAL1.pin_1, C1.1
  N3: IC3.PD5(T1), L298N1.ENA
  N4: IC3.PB1(OC1A), Part2.CS
  N5: IC3.PB2(SS_OC1B), Part2.CE
  N6: IC3.PB3(MOSI_OC2), Part2.MOSI
  N7: IC3.PB4(MISO), Part2.MISO
  N8: IC3.PB5(SCK), Part2.SCK
  N9: IC3.PC0(ADC0), L298N1.IN2
  N10: IC3.PC1(ADC1), L298N1.5V#9, L298N1.IN1
  N11: L298N1.OUT3, M1.pin_2
  N12: L298N1.OUT4, M1.pin_1
  N13: L298N1.12V, VCC1.+, IC4.IN
  N14: U3.NSS, Jetson_Nano1.3V3
  N15: U3.SCK, Jetson_Nano1.GPIO24
  N16: U3.MOSI, Jetson_Nano1.GPIO25
  N17: U3.MISO, U3.RST, Jetson_Nano1.GND

notes:
  spi 1
  23 clock white
  21 miso yellow
  19 mosi brown
  24 select0 green
  26 select1orange
  12 rest pink
  RFID 1
  spi 1
  23 clock white
  21 miso yellow
  19 mosi brown
  24 select0 green
  12 rest pink

custom parts:
  Atmega8: MICROCONTROLLER 8 Kbytes FLASH 1 kbytes SRAM 512 bytes EEPROM USART 4-channel 10 bit ADC 2-channel 8 bit ADC
  L298N DC motor driver: 2x DC motor driver with 78M05 positive voltage regulator (7..35 V) L298N: max 46 V, 2 A Set 5 V Enable jumper to enable 5 V regultor (needed for the L298N) and +5 V output at screw terminal or supply external +5 V at screw terminal Set ENA and/or ENB to +5 V to enable motor permanently or supply ENA and/or ENB with PWM signal IN1 and IN2 set rotation directory for motor A (OUT1/OUT2) IN2 and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
  RFID RC522 SIP - 8 pins: A SIP stand-in part for RFID RC522 . With 8 pins on a 300 mil single inline package (SIP) footprint.
