# Fritzing sketch rfid_3 (saved by Fritzing 0.9.5d)
breadboards: 1

parts:
  U1 = RFID RC522 SIP - 8 pins [chip_label="RFID RC522" package="SIP (Single Inline) [THT]"]
  Jetson_Nano1 = Jetson Nano
  C3 = Electrolytic Capacitor [capacitance=10μF package="0605 [SMD, electrolytic]"]

nets:
  N1: U1.NSS, Jetson_Nano1.GPIO11
  N2: U1.SCK, Jetson_Nano1.ID_SC
  N3: U1.MOSI, Jetson_Nano1.5V
  N4: U1.MISO, Jetson_Nano1.GPIO10
  N5: U1.GND, Jetson_Nano1.GPIO19, C3.-
  N6: U1.RST, Jetson_Nano1.GPIO5
  N7: U1.VCC, Jetson_Nano1.GPIO21, C3.+

notes:
  spi 2
  13 clock white
  22 miso yellow
  37 mosi brown
  18 select0 green
  16 select1orange
  12 rest pink
  NRF24
  40 IRQ blue
  spi 2
  13 clock white
  22 miso yellow
  37 mosi brown
  18 select0 green
  12 rest pink
  NRF24
  40 IRQ blue

custom parts:
  RFID RC522 SIP - 8 pins: A SIP stand-in part for RFID RC522 . With 8 pins on a 300 mil single inline package (SIP) footprint.
